# Fritzing sketch Esquema (saved by Fritzing 0.9.2b)
breadboards: 1

parts:
  Parte2 = Arduino Uno (Rev3)
  LED2 = LED - 5mm [color="Red (633nm)" package="5 mm [THT]"]
  R3 = Resistor [tolerance=±5% resistance=1k package=THT]  # not connected
  S2 = Pushbutton [package=THT]
  R4 = Resistor [tolerance=±5% resistance=1k package=THT]

nets:
  N1: Parte2.D8, S2.leg1, R4.Pin_1
  N2: Parte2.D4, LED2.anode
  N3: Parte2.5V, S2.leg0
  N4: Parte2.GND, R4.Pin_0
